// Logisim project ALU_template.circ as structural Verilog: 15 circuits, main circuit ALU32
module LeftShift32 (
  input  [31:0] B,
  input  Cin,
  input  [4:0] Sa,
  output [31:0] C
);

  wire [31:0] multiplexer_1_out, multiplexer_2_out, multiplexer_3_out, multiplexer_4_out, shift1b_1_c,
       shift2b_1_c, shift4b_1_c, shift8b_1_c, shift16b_1_c;

  Multiplexer #(.width(32), .enable("false")) multiplexer_1 (
    .in0(B), .in1(shift1b_1_c), .out(multiplexer_1_out), .sel(Sa[0]));
  Shift1b shift1b_1 (.Cin(Cin), .B(B), .C(shift1b_1_c));
  Shift2b shift2b_1 (.Cin(Cin), .B(multiplexer_1_out), .C(shift2b_1_c));
  Multiplexer #(.width(32), .enable("false")) multiplexer_2 (
    .in0(multiplexer_1_out), .in1(shift2b_1_c), .out(multiplexer_2_out), .sel(Sa[1]));
  Shift4b shift4b_1 (.Cin(Cin), .B(multiplexer_2_out), .C(shift4b_1_c));
  Multiplexer #(.width(32), .enable("false")) multiplexer_3 (
    .in0(multiplexer_2_out), .in1(shift4b_1_c), .out(multiplexer_3_out), .sel(Sa[2]));
  Shift8b shift8b_1 (.Cin(Cin), .B(multiplexer_3_out), .C(shift8b_1_c));
  Multiplexer #(.width(32), .enable("false")) multiplexer_4 (
    .in0(multiplexer_3_out), .in1(shift8b_1_c), .out(multiplexer_4_out), .sel(Sa[3]));
  Shift16b shift16b_1 (.Cin(Cin), .B(multiplexer_4_out), .C(shift16b_1_c));
  Multiplexer #(.width(32), .enable("false")) multiplexer_5 (
    .in0(multiplexer_4_out), .in1(shift16b_1_c), .out(C), .sel(Sa[4]));

  // Notes on the sheet:
  //   Do not delete or rename any of the input or output pins, and do not add any other pins.
  //   (It's fine to move them around, though)
endmodule

module Add32 (
  input  [31:0] A,
  input  [31:0] B,
  input  Cin,
  output V,
  output [31:0] C
);

  wire adder16bit_1_cout, adder16bit_2_cout, adder16bit_2_overflow;

  Adder16bit adder16bit_1 (
    .A16(A[15:0]), .B16(B[15:0]), .Cin(Cin), .Cout(adder16bit_1_cout), .S16(C[15:0]));  // open: Overflow
  Adder16bit adder16bit_2 (
    .A16(A[31:16]), .B16(B[31:16]), .Cin(adder16bit_1_cout), .Cout(adder16bit_2_cout),
    .Overflow(adder16bit_2_overflow), .S16(C[31:16]));
  xor xor_1 (V, adder16bit_2_cout, adder16bit_2_overflow);

  // Notes on the sheet:
  //   Do not delete or rename any of the input or output pins, and do not add any other pins.
  //   (It's fine to move the pins around, though)
endmodule

module ALU32 (
  input  [31:0] A,
  input  [31:0] B,
  input  [3:0] Op,
  input  [4:0] Sa,
  output [31:0] C,
  output V
);

  wire and_1_out, and_4_out;
  wire [31:0] add32_1_c, and_2_out, and_3_out, bit_extender_1_out, compare32_1_c, logicgate32_1_c,
       multiplexer_1_out, not_1_out, shiftcircuit_1_c;

  assign not_1_out = ~B;  // NOT_Gate not_1, 32 bits wide
  and and_1 (and_1_out, Op[1], ~Op[3]);  // AND_Gate
  Multiplexer #(.width(32), .enable("false")) multiplexer_1 (
    .in0(B), .in1(not_1_out), .out(multiplexer_1_out), .sel(Op[2]));
  assign and_2_out = A & bit_extender_1_out;  // AND_Gate and_2, 32 bits wide
  assign bit_extender_1_out = {{31{and_1_out}}, and_1_out};  // Bit_Extender bit_extender_1
  assign and_3_out = bit_extender_1_out & multiplexer_1_out;  // AND_Gate and_3, 32 bits wide
  and and_4 (and_4_out, and_1_out, Op[2]);
  LogicGate32 logicgate32_1 (.A(A), .B(B), .Op(Op), .C(logicgate32_1_c));
  Add32 add32_1 (.A(and_2_out), .B(and_3_out), .Cin(and_4_out), .V(V), .C(add32_1_c));
  Compare32 compare32_1 (.B(B), .A(A), .Op(Op), .C(compare32_1_c));
  ShiftCircuit shiftcircuit_1 (.B(B), .Op(Op), .Sa(Sa), .C(shiftcircuit_1_c));
  assign C = logicgate32_1_c | add32_1_c | compare32_1_c | shiftcircuit_1_c;  // OR_Gate or_1, 32 bits wide

  // Notes on the sheet:
  //   (It's fine to move the pins around, though)
  //   Do not delete or rename any of the input or output pins, and do not add any other pins.
endmodule

module Shift1b (
  input  Cin,
  input  [31:0] B,
  output [31:0] C
);


  assign C = {B[30:0], Cin};
endmodule

module Shift2b (
  input  Cin,
  input  [31:0] B,
  output [31:0] C
);

  wire [31:0] shift1b_1_c;

  Shift1b shift1b_1 (.Cin(Cin), .B(B), .C(shift1b_1_c));
  Shift1b shift1b_2 (.Cin(Cin), .B(shift1b_1_c), .C(C));
endmodule

module Shift4b (
  input  Cin,
  input  [31:0] B,
  output [31:0] C
);

  wire [31:0] shift2b_1_c;

  Shift2b shift2b_1 (.Cin(Cin), .B(B), .C(shift2b_1_c));
  Shift2b shift2b_2 (.Cin(Cin), .B(shift2b_1_c), .C(C));
endmodule

module Shift8b (
  input  Cin,
  input  [31:0] B,
  output [31:0] C
);

  wire [31:0] shift4b_1_c;

  Shift4b shift4b_1 (.Cin(Cin), .B(B), .C(shift4b_1_c));
  Shift4b shift4b_2 (.Cin(Cin), .B(shift4b_1_c), .C(C));
endmodule

module Shift16b (
  input  Cin,
  input  [31:0] B,
  output [31:0] C
);

  wire [31:0] shift8b_1_c;

  Shift8b shift8b_1 (.Cin(Cin), .B(B), .C(shift8b_1_c));
  Shift8b shift8b_2 (.Cin(Cin), .B(shift8b_1_c), .C(C));
endmodule

module Adder1bit (
  input  A,
  input  B,
  input  Cin,
  output S,
  output Cout
);

  wire and_1_out, and_2_out, xor_1_out;

  xor xor_1 (xor_1_out, A, B);
  and and_1 (and_1_out, xor_1_out, Cin);
  and and_2 (and_2_out, A, B);
  xor xor_2 (S, xor_1_out, Cin);
  or or_1 (Cout, and_1_out, and_2_out);
endmodule

module Adder16bit (
  input  [15:0] A16,
  input  [15:0] B16,
  input  Cin,
  output Cout,
  output Overflow,
  output [15:0] S16
);

  wire add4bit_1_cout, add4bit_2_cout, add4bit_3_cout;

  add4bit add4bit_1 (.B4(B16[3:0]), .Cout(add4bit_1_cout), .A4(A16[3:0]), .Cin(Cin), .S4(S16[3:0]));  // open: Overflow
  add4bit add4bit_2 (
    .B4(B16[7:4]), .Cout(add4bit_2_cout), .A4(A16[7:4]), .Cin(add4bit_1_cout), .S4(S16[7:4]));  // open: Overflow
  add4bit add4bit_3 (
    .B4(B16[11:8]), .Cout(add4bit_3_cout), .A4(A16[11:8]), .Cin(add4bit_2_cout), .S4(S16[11:8]));  // open: Overflow
  add4bit add4bit_4 (
    .Overflow(Overflow), .B4(B16[15:12]), .Cout(Cout), .A4(A16[15:12]), .Cin(add4bit_3_cout), .S4(S16[15:12]));
endmodule

module add4bit (
  input  [3:0] B4,
  input  [3:0] A4,
  input  Cin,
  output Cout,
  output Overflow,
  output [3:0] S4
);

  wire adder1bit_1_cout, adder1bit_2_cout;

  Adder1bit adder1bit_1 (.Cout(adder1bit_1_cout), .A(A4[0]), .S(S4[0]), .B(B4[0]), .Cin(Cin));
  Adder1bit adder1bit_2 (.Cout(adder1bit_2_cout), .A(A4[1]), .S(S4[1]), .B(B4[1]), .Cin(adder1bit_1_cout));
  Adder1bit adder1bit_3 (.Cout(Overflow), .A(A4[2]), .S(S4[2]), .B(B4[2]), .Cin(adder1bit_2_cout));
  Adder1bit adder1bit_4 (.Cout(Cout), .A(A4[3]), .S(S4[3]), .B(B4[3]), .Cin(Overflow));
endmodule

module ShiftCircuit (
  input  [31:0] B,
  input  [3:0] Op,
  input  [4:0] Sa,
  output [31:0] C
);

  wire and_1_out, and_2_out, and_3_out, mirror_1_signbit, not_1_out, xnor_1_out;
  wire [4:0] and_4_out, bit_extender_1_out;
  wire [31:0] leftshift32_1_c, mirror_1_b_mirror, mirror_2_b_mirror, multiplexer_1_out;

  Mirror mirror_1 (.B(B), .B_mirror(mirror_1_b_mirror), .Signbit(mirror_1_signbit));
  and and_1 (and_1_out, mirror_1_signbit, Op[0]);
  not not_1 (not_1_out, Op[1]);
  xnor xnor_1 (xnor_1_out, Op[2], Op[3]);
  Multiplexer #(.width(32)) multiplexer_1 (
    .in0(B), .in1(mirror_1_b_mirror), .out(multiplexer_1_out), .sel(Op[3]), .en(and_2_out));
  and and_2 (and_2_out, not_1_out, xnor_1_out);
  and and_3 (and_3_out, and_1_out, Op[3]);
  assign bit_extender_1_out = {{4{and_2_out}}, and_2_out};  // Bit_Extender bit_extender_1
  assign and_4_out = bit_extender_1_out & Sa;  // AND_Gate and_4, 5 bits wide
  LeftShift32 leftshift32_1 (.B(multiplexer_1_out), .Cin(and_3_out), .Sa(and_4_out), .C(leftshift32_1_c));
  Multiplexer #(.width(32), .enable("false")) multiplexer_2 (
    .in0(leftshift32_1_c), .in1(mirror_2_b_mirror), .out(C), .sel(Op[3]));
  Mirror mirror_2 (.B(leftshift32_1_c), .B_mirror(mirror_2_b_mirror));  // open: Signbit
endmodule

module Mirror (
  input  [31:0] B,
  output [31:0] B_mirror,
  output Signbit
);


  assign B_mirror = {B[0], B[1], B[2], B[3], B[4], B[5], B[6], B[7], B[8], B[9], B[10], B[11], B[12], B[13], B[14], B[15], B[16], B[17], B[18], B[19], B[20], B[21], B[22], B[23], B[24], B[25], B[26], B[27], B[28], B[29], B[30], B[31]};
  assign Signbit = B[31];
endmodule

module LogicGate32 (
  input  [31:0] A,
  input  [31:0] B,
  input  [3:0] Op,
  output [31:0] C
);

  wire and_1_out, xnor_1_out, xor_1_out;
  wire [31:0] and_2_out, nor_1_out, or_1_out, xor_2_out;

  xor xor_1 (xor_1_out, Op[2], Op[3]);
  xnor xnor_1 (xnor_1_out, Op[3], Op[1]);
  and and_1 (and_1_out, xor_1_out, xnor_1_out);
  assign and_2_out = A & B;  // AND_Gate and_2, 32 bits wide
  assign or_1_out = A | B;  // OR_Gate or_1, 32 bits wide
  assign xor_2_out = A ^ B;  // XOR_Gate xor_2, 32 bits wide
  assign nor_1_out = ~(A | B);  // NOR_Gate nor_1, 32 bits wide
  Multiplexer #(.select(2), .width(32)) multiplexer_1 (
    .in0(and_2_out), .in1(or_1_out), .in2(xor_2_out), .in3(nor_1_out), .out(C), .sel(Op[1:0]), .en(and_1_out));
endmodule

module Compare32 (
  input  [31:0] B,
  input  [31:0] A,
  input  [3:0] Op,
  output [31:0] C
);

  wire and_3_out, and_6_out, and_7_out, and_8_out, not_2_out, not_3_out, xnor_2_out;
  wire [1:0] and_4_out, and_5_out;
  wire [7:0] and_1_out, and_2_out;
  wire [31:0] bit_extender_1_out, bit_extender_2_out, bit_extender_3_out, bit_extender_4_out, not_1_out,
       xnor_1_out;

  assign not_1_out = ~A;  // NOT_Gate not_1, 32 bits wide
  assign xnor_1_out = ~(B ^ A);  // XNOR_Gate xnor_1, 32 bits wide
  xnor xnor_2 (xnor_2_out, Op[1], Op[2]);
  assign and_1_out = xnor_1_out[7:0] & xnor_1_out[15:8] & xnor_1_out[23:16] & xnor_1_out[31:24];  // AND_Gate and_1, 8 bits wide
  assign and_2_out = not_1_out[7:0] & not_1_out[15:8] & not_1_out[23:16] & not_1_out[31:24];  // AND_Gate and_2, 8 bits wide
  and and_3 (and_3_out, Op[3], xnor_2_out);
  assign and_4_out = and_2_out[1:0] & and_2_out[3:2] & and_2_out[5:4] & and_2_out[7:6];  // AND_Gate and_4, 2 bits wide
  assign and_5_out = and_1_out[1:0] & and_1_out[3:2] & and_1_out[5:4] & and_1_out[7:6];  // AND_Gate and_5, 2 bits wide
  and and_6 (and_6_out, and_4_out[0], and_4_out[1]);
  and and_7 (and_7_out, and_5_out[0], and_5_out[1]);
  and and_8 (and_8_out, ~A[31], ~and_6_out);  // AND_Gate
  not not_2 (not_2_out, and_7_out);
  not not_3 (not_3_out, and_8_out);
  assign bit_extender_1_out = {{31{1'b0}}, not_2_out};  // Bit_Extender bit_extender_1
  assign bit_extender_2_out = {{31{1'b0}}, and_7_out};  // Bit_Extender bit_extender_2
  assign bit_extender_3_out = {{31{1'b0}}, not_3_out};  // Bit_Extender bit_extender_3
  assign bit_extender_4_out = {{31{1'b0}}, and_8_out};  // Bit_Extender bit_extender_4
  Multiplexer #(.select(2), .width(32)) multiplexer_1 (
    .in0(bit_extender_1_out), .in1(bit_extender_2_out), .in2(bit_extender_3_out), .in3(bit_extender_4_out),
    .out(C), .sel(Op[1:0]), .en(and_3_out));
endmodule
