// Logisim project RISCV32.circ as structural Verilog: 12 circuits, main circuit RISCV32
module RISCV32 (
  input  in_1
);

  wire Clk, comparator_black_box_1_p4, isLUI, split_1_byte, split_1_load, split_1_slt, split_1_store,
       split_1_useimm, split_1_usemem, split_1_we;
  wire [3:0] SelectByte, split_1_aluop;
  wire [4:0] alu_1_p4, multiplexer_1_out, SA, split_1_rd, split_1_rs1, split_1_rs2;
  wire [31:0] add4_1_pc4, alu_1_p5, B, bit_extender_2_out, DataIN, loadbyte_1_load_data, multiplexer_2_out,
       multiplexer_4_out, Op, PC_q, RAW, registerfile_1_p1, registerfile_1_p7, split_1_imm;
  wire [31:5] multiplexer_1_out_2;

  Register #(.width(32)) PC (.D(add4_1_pc4), .clk(Clk), .Q(PC_q), .clr(in_1));  // open: en
  Clock clock_1 (.out(Clk));
  ADD4 add4_1 (.PC(PC_q), .PC4(add4_1_pc4));
  // RISC_VProgramROM risc_vprogramrom_1: pin names not known; wires that end beside it: PC_q, Op[31:7], Op
  assign SA = {{1{1'b0}}, {Op[0], Op[1], Op[3], Op[6]}};  // Bit_Extender bit_extender_1
  SPLIT split_1 (
    .OP(Op), .WE(split_1_we), .RD(split_1_rd), .RS1(split_1_rs1), .RS2(split_1_rs2), .IMM(split_1_imm),
    .USEIMM(split_1_useimm), .ALUOP(split_1_aluop), .SLT(split_1_slt), .BYTE(split_1_byte),
    .LOAD(split_1_load), .STORE(split_1_store), .useMEM(split_1_usemem), .isLUI(isLUI));
  // RegisterFile registerfile_1: pin names not known; wires that end beside it: registerfile_1_p1, Clk, split_1_we, split_1_rd, split_1_rs1, split_1_rs2, registerfile_1_p7, B
  Multiplexer #(.width(32), .enable("false")) multiplexer_1 (
    .in0(B), .in1(split_1_imm), .out({multiplexer_1_out_2, multiplexer_1_out}), .sel(split_1_useimm));
  Multiplexer #(.width(32), .enable("false")) multiplexer_2 (
    .in0(registerfile_1_p7), .in1({multiplexer_1_out_2, multiplexer_1_out}), .out(multiplexer_2_out),
    .sel(isLUI));
  // ALU alu_1: pin names not known; wires that end beside it: multiplexer_2_out, {multiplexer_1_out_2, multiplexer_1_out}, split_1_aluop, alu_1_p4, alu_1_p5
  // Comparator_Black_Box comparator_black_box_1: pin names not known; wires that end beside it: registerfile_1_p7, {multiplexer_1_out_2, multiplexer_1_out}, split_1_slt, comparator_black_box_1_p4
  Multiplexer #(.width(5), .enable("false")) multiplexer_3 (
    .in0(multiplexer_1_out), .in1(SA), .out(alu_1_p4), .sel(isLUI));
  assign bit_extender_2_out = {{31{1'b0}}, comparator_black_box_1_p4};  // Bit_Extender bit_extender_2
  DATA_IN data_in_1 (.B(B), .SelectByte(SelectByte), .STORE(split_1_store), .BYTE(split_1_byte), .Data_in(DataIN));
  Multiplexer #(.width(32), .enable("false")) multiplexer_4 (
    .in0(alu_1_p5), .in1(bit_extender_2_out), .out(multiplexer_4_out), .sel(split_1_slt));
  SelectByte selectbyte_1 (
    .num1(Op[0]), .num0(Op[6]), .Byte(split_1_byte), .First2bit(multiplexer_4_out[1:0]),
    .SelectByte(SelectByte));
  RAM ram_1 (
    .addr(multiplexer_4_out[9:2]), .data(RAW[7:0]), .sel(SelectByte[0]), .clk(Clk), .ld(split_1_load),
    .clr(in_1));
  Multiplexer #(.width(32), .enable("false")) multiplexer_5 (
    .in0(multiplexer_4_out), .in1(loadbyte_1_load_data), .out(registerfile_1_p1), .sel(split_1_usemem));
  LOADBYTE loadbyte_1 (.RAWData(RAW), .SelectByte(SelectByte), .BYTE(split_1_byte), .LOAD_Data(loadbyte_1_load_data));
  // Pins of 8 and 20 bits meet at multiplexer_4_out[21:2]
  // Pins of 8 and 32 bits meet at RAW
  // Pins of 1 and 4 bits meet at SelectByte

  // Other names for the same wires on the sheet: Clr = in_1

  // Notes on the sheet:
  //   contents of risc_vprogramrom_1 (hex, n*v repeats v):
  //   addi x1, x0, 0x123 addi x2, x0, 0x456 add x3, x1, x2 sub x4, x3, x1  #LOGICAL OPERATIONS and x5, x2,
  //   x3 andi x6, x1, 0x0f0 or x7, x2, x1 ori x8, x3, 0xcf0 xor x9, x7, x3 xori x10, x3, 0xdef  #SHIFTING
  //   OPERATORS addi x11, x0, 0x0ff addi x12, x0, 25 sll x13, x11, x12 sll x14, x13, x12 addi x12, x0, 23
  //   sra x15, x14, x12  #LUI OPERATORS lui x16, 0x23233 addi x16, x16, 0x501 lui x17, 0x9267 addi x17,
  //   x17, 0x405  #COMPARATOR slt x18, x2, x3 slt x19, x1, x2  #STORE + LOAD OPERATIONS sb x17, 3(x0) sw
  //   x15, 4(x0) lb x20, 6(x0) lw x21, 8(x0)
  //   Mux1
  //   Mux2
  //   Mux3
  //   Mux4
  //   Mux5
endmodule

module ADD4 (
  input  [31:0] PC,
  output [31:0] PC4
);

  // Incrementer #(.width(30)) incrementer_1: pin names not known; wires that end beside it: PC[31:2], PC4[31:2]

  assign PC4[1:0] = PC[1:0];
endmodule

module SPLIT (
  input  [31:0] OP,
  output WE,
  output [4:0] RD,
  output [4:0] RS1,
  output [4:0] RS2,
  output [31:0] IMM,
  output USEIMM,
  output [3:0] ALUOP,
  output SLT,
  output BYTE,
  output LOAD,
  output STORE,
  output useMEM,
  output isLUI
);

  wire opcode_1_isarith, opcode_1_isimm;

  OPCODE opcode_1 (
    .OpCode(OP[6:0]), .isLUI(isLUI), .isLOAD(LOAD), .isSTORE(STORE), .isIMM(opcode_1_isimm),
    .isARITH(opcode_1_isarith));
  REGISTER_Signal register_signal_1 (
    .isSTORE(STORE), .isLUI(isLUI), .isLOAD(LOAD), .isIMM(opcode_1_isimm), .isARITH(opcode_1_isarith),
    .Bit7_31(OP[31:7]), .RegWrite(WE), .rd(RD), .rs1(RS1), .rs2(RS2));
  IMM imm_1 (
    .Bit7_31(OP[31:7]), .isLUI(isLUI), .isLOAD(LOAD), .isIMM(opcode_1_isimm), .isSTORE(STORE), .IMM(IMM),
    .USEIMM(USEIMM));
  ALUandMEM aluandmem_1 (
    .Bit7_31(OP[31:7]), .isARITH(opcode_1_isarith), .isIMM(opcode_1_isimm), .isLOAD(LOAD), .isSTORE(STORE),
    .isLUI(isLUI), .ALUOPERATION(ALUOP), .SLT(SLT), .isBYTE(BYTE));
  or or_1 (useMEM, LOAD, STORE);
endmodule

module OPCODE (
  input  [6:0] OpCode,
  output isLUI,
  output isLOAD,
  output isSTORE,
  output isIMM,
  output isARITH
);

  and LUIop (isLUI, OpCode[0], OpCode[1], OpCode[2], ~OpCode[3], OpCode[4], OpCode[5], ~OpCode[6]);  // AND_Gate
  and LOAD (isLOAD, OpCode[0], OpCode[1], ~OpCode[2], ~OpCode[3], ~OpCode[4], ~OpCode[5], ~OpCode[6]);  // AND_Gate
  and STORE (isSTORE, OpCode[0], OpCode[1], ~OpCode[2], ~OpCode[3], ~OpCode[4], OpCode[5], ~OpCode[6]);  // AND_Gate
  and IMMop (isIMM, OpCode[0], OpCode[1], ~OpCode[2], ~OpCode[3], OpCode[4], ~OpCode[5], ~OpCode[6]);  // AND_Gate
  and ARITH (isARITH, OpCode[0], OpCode[1], ~OpCode[2], ~OpCode[3], OpCode[4], OpCode[5], ~OpCode[6]);  // AND_Gate
endmodule

module REGISTER_Signal (
  input  isSTORE,
  input  isLUI,
  input  isLOAD,
  input  isIMM,
  input  isARITH,
  input  [24:0] Bit7_31,
  output RegWrite,
  output [4:0] rd,
  output [4:0] rs1,
  output [4:0] rs2
);

  wire and_2_out, and_3_out, or_1_out, or_2_out, or_3_out, or_4_out;
  wire [4:0] bit_extender_1_out, bit_extender_2_out, bit_extender_3_out;

  and and_1 (RegWrite, ~isSTORE, or_1_out);  // AND_Gate
  or or_1 (or_1_out, isLUI, isLOAD, isIMM, isARITH);
  or or_2 (or_2_out, isSTORE, isLOAD, isIMM, isARITH);
  or or_3 (or_3_out, isLUI, isLOAD, isIMM);
  or or_4 (or_4_out, isSTORE, isARITH);
  assign bit_extender_1_out = {{4{RegWrite}}, RegWrite};  // Bit_Extender bit_extender_1
  and and_2 (and_2_out, ~isLUI, or_2_out);  // AND_Gate
  assign bit_extender_2_out = {{4{and_2_out}}, and_2_out};  // Bit_Extender bit_extender_2
  and and_3 (and_3_out, ~or_3_out, or_4_out);  // AND_Gate
  assign rd = bit_extender_1_out & Bit7_31[4:0];  // AND_Gate and_4, 5 bits wide
  assign rs1 = bit_extender_2_out & Bit7_31[12:8];  // AND_Gate and_5, 5 bits wide
  assign bit_extender_3_out = {{4{and_3_out}}, and_3_out};  // Bit_Extender bit_extender_3
  assign rs2 = bit_extender_3_out & Bit7_31[17:13];  // AND_Gate and_6, 5 bits wide
endmodule

module IMM (
  input  [24:0] Bit7_31,
  input  isLUI,
  input  isLOAD,
  input  isIMM,
  input  isSTORE,
  output [31:0] IMM,
  output USEIMM
);

  wire or_1_out;
  wire [11:0] and_2_out, and_3_out, bit_extender_2_out, bit_extender_3_out;
  wire [19:0] and_1_out, bit_extender_1_out;
  wire [31:0] bit_extender_4_out, bit_extender_5_out, bit_extender_6_out;

  or or_1 (or_1_out, isLOAD, isIMM);
  or or_2 (USEIMM, isLUI, isLOAD, isIMM, isSTORE);
  assign bit_extender_1_out = {{19{isLUI}}, isLUI};  // Bit_Extender bit_extender_1
  assign bit_extender_2_out = {{11{or_1_out}}, or_1_out};  // Bit_Extender bit_extender_2
  assign bit_extender_3_out = {{11{isSTORE}}, isSTORE};  // Bit_Extender bit_extender_3
  assign and_1_out = Bit7_31[24:5] & bit_extender_1_out;  // AND_Gate and_1, 20 bits wide
  assign and_2_out = Bit7_31[24:13] & bit_extender_2_out;  // AND_Gate and_2, 12 bits wide
  assign and_3_out = {Bit7_31[24:18], Bit7_31[4:0]} & bit_extender_3_out;  // AND_Gate and_3, 12 bits wide
  assign bit_extender_4_out = {{12{and_1_out[19]}}, and_1_out};  // Bit_Extender bit_extender_4
  assign bit_extender_5_out = {{20{and_2_out[11]}}, and_2_out};  // Bit_Extender bit_extender_5
  assign bit_extender_6_out = {{20{and_3_out[11]}}, and_3_out};  // Bit_Extender bit_extender_6
  assign IMM = bit_extender_4_out | bit_extender_5_out | bit_extender_6_out;  // OR_Gate or_3, 32 bits wide

  // Other names for the same wires on the sheet: bit0_4[4:0] = Bit7_31[4:0]
endmodule

module ALUandMEM (
  input  [24:0] Bit7_31,
  input  isARITH,
  input  isIMM,
  input  isLOAD,
  input  isSTORE,
  input  isLUI,
  output [3:0] ALUOPERATION,
  output SLT,
  output isBYTE
);

  wire and_1_out, and_2_out, ARITHorIMM, not_1_out, or_1_out, or_2_out;
  wire [3:0] arith_op_1_aluop, bit_extender_1_out, bit_extender_2_out, imm_op_1_aluop, multiplexer_1_out,
       multiplexer_2_out;
  wire [3:2] not_2_out;

  or or_1 (or_1_out, isLOAD, isSTORE);
  assign bit_extender_1_out = {{3{isLUI}}, isLUI};  // Bit_Extender bit_extender_1
  or or_2 (or_2_out, isLOAD, isSTORE);
  not not_1 (not_1_out, or_2_out);
  or or_3 (ARITHorIMM, isARITH, isIMM);
  and and_1 (and_1_out, Bit7_31[23], isARITH);
  assign bit_extender_2_out = {{3{1'b0}}, not_1_out};  // Bit_Extender bit_extender_2
  not not_2 (not_2_out[2], bit_extender_1_out[2]);
  not not_3 (not_2_out[3], bit_extender_1_out[3]);
  and and_2 (and_2_out, ~Bit7_31[5], Bit7_31[6], ~Bit7_31[7]);  // AND_Gate
  and and_3 (isBYTE, ~Bit7_31[5], ~Bit7_31[6], ~Bit7_31[7]);  // AND_Gate
  ARITH_OP arith_op_1 (.funct3(Bit7_31[7:5]), .ARITHOp(and_1_out), .ALUop(arith_op_1_aluop));
  IMM_OP imm_op_1 (.funct3(Bit7_31[7:5]), .IMMop(isIMM), .ALUOp(imm_op_1_aluop));
  and and_4 (SLT, and_2_out, ARITHorIMM);
  Multiplexer #(.width(4), .enable("false")) multiplexer_1 (
    .in0(arith_op_1_aluop), .in1(imm_op_1_aluop), .out(multiplexer_1_out), .sel(isIMM));
  Multiplexer #(.width(4), .enable("false")) multiplexer_2 (
    .in0(multiplexer_1_out), .in1(bit_extender_2_out), .out(multiplexer_2_out), .sel(or_1_out));
  Multiplexer #(.width(4), .enable("false")) multiplexer_3 (
    .in0(multiplexer_2_out), .in1({not_2_out, bit_extender_1_out[1:0]}), .out(ALUOPERATION), .sel(isLUI));
endmodule

module ARITH_OP (
  input  [2:0] funct3,
  input  ARITHOp,
  output [3:0] ALUop
);

  wire not_1_out;

  or or_1 (ALUop[1], funct3[1], funct3[0]);
  or or_2 (ALUop[2], ARITHOp, funct3[2]);
  not not_1 (not_1_out, ARITHOp);
  and and_1 (ALUop[3], funct3[2], not_1_out);

  assign ALUop[0] = funct3[0];
endmodule

module IMM_OP (
  input  [2:0] funct3,
  input  IMMop,
  output [3:0] ALUOp
);


  assign ALUOp = {{2{funct3[2]}}, funct3[1:0]};
endmodule

module SelectByte (
  input  num1,
  input  num0,
  input  Byte,
  input  [1:0] First2bit,
  output [3:0] SelectByte
);

  wire [3:0] multiplexer_1_out;

  Multiplexer #(.select(2), .width(4), .enable("false")) multiplexer_1 (
    .in0({{3{num0}}, num1}), .in1({{2{num0}}, num1, num0}), .in2({num0, num1, {2{num0}}}),
    .in3({num1, {3{num0}}}), .out(multiplexer_1_out), .sel(First2bit));
  Multiplexer #(.width(4), .enable("false")) multiplexer_2 (
    .in0({4{num1}}), .in1(multiplexer_1_out), .out(SelectByte), .sel(Byte));

  // Notes on the sheet:
  //   1111
  //   0001
  //   0010
  //   0100
  //   1000
endmodule

module DATA_IN (
  input  [31:0] B,
  input  [3:0] SelectByte,
  input  STORE,
  input  BYTE,
  output [31:0] Data_in
);

  wire and_1_out, not_1_out, not_2_out, not_3_out;
  wire [1:0] or_1_out;
  wire [7:0] bit_extender_4_out;
  wire [15:0] bit_extender_3_out, bit_extender_5_out;
  wire [23:0] bit_extender_2_out, bit_extender_6_out;
  wire [31:0] bit_extender_1_out, multiplexer_1_out;

  assign bit_extender_1_out = {{24{1'b0}}, B[7:0]};  // Bit_Extender bit_extender_1
  assign bit_extender_2_out = {{16{1'b0}}, B[7:0]};  // Bit_Extender bit_extender_2
  not not_1 (not_1_out, BYTE);
  assign bit_extender_3_out = {{8{1'b0}}, B[7:0]};  // Bit_Extender bit_extender_3
  not not_2 (not_2_out, BYTE);
  not not_3 (not_3_out, BYTE);
  assign bit_extender_4_out = {{7{1'b0}}, not_1_out};  // Bit_Extender bit_extender_4
  assign bit_extender_5_out = {{15{1'b0}}, not_2_out};  // Bit_Extender bit_extender_5
  assign bit_extender_6_out = {{23{1'b0}}, not_3_out};  // Bit_Extender bit_extender_6
  or or_1 (or_1_out[0], SelectByte[1], SelectByte[3]);
  or or_2 (or_1_out[1], SelectByte[2], SelectByte[3]);
  Multiplexer #(.select(2), .width(32), .enable("false")) multiplexer_1 (
    .in0(bit_extender_1_out), .in1({bit_extender_2_out, bit_extender_4_out}),
    .in2({bit_extender_3_out, bit_extender_5_out}), .in3({B[7:0], bit_extender_6_out}),
    .out(multiplexer_1_out), .sel(or_1_out));
  Multiplexer #(.width(32), .enable("false")) multiplexer_2 (
    .in0(B), .in1(multiplexer_1_out), .out(Data_in), .sel(and_1_out));
  and and_1 (and_1_out, STORE, BYTE);
endmodule

module LOADBYTE (
  input  [31:0] RAWData,
  input  [3:0] SelectByte,
  input  BYTE,
  output [31:0] LOAD_Data
);

  wire [1:0] or_1_out;
  wire [31:0] bit_extender_1_out, bit_extender_2_out, bit_extender_3_out, bit_extender_4_out,
       multiplexer_1_out;

  or or_1 (or_1_out[0], SelectByte[1], SelectByte[3]);
  or or_2 (or_1_out[1], SelectByte[2], SelectByte[3]);
  assign bit_extender_1_out = {{24{RAWData[7]}}, RAWData[7:0]};  // Bit_Extender bit_extender_1
  assign bit_extender_2_out = {{24{RAWData[15]}}, RAWData[15:8]};  // Bit_Extender bit_extender_2
  assign bit_extender_3_out = {{24{RAWData[23]}}, RAWData[23:16]};  // Bit_Extender bit_extender_3
  assign bit_extender_4_out = {{24{RAWData[31]}}, RAWData[31:24]};  // Bit_Extender bit_extender_4
  Multiplexer #(.select(2), .width(32), .enable("false")) multiplexer_1 (
    .in0(bit_extender_1_out), .in1(bit_extender_2_out), .in2(bit_extender_3_out), .in3(bit_extender_4_out),
    .out(multiplexer_1_out), .sel(or_1_out));
  Multiplexer #(.width(32), .enable("false")) multiplexer_2 (
    .in0(RAWData), .in1(multiplexer_1_out), .out(LOAD_Data), .sel(BYTE));
endmodule
